// Logisim project TallerEvolution.circ as structural Verilog: 12 circuits, main circuit sumador_simple
module sumador_simple (
  input  A,
  input  B,
  output S,
  output Cout
);

  xor xor_1 (S, A, B);
  and and_1 (Cout, A, B);
endmodule

module sumador_completo (
  input  Cin,
  input  A,
  input  B,
  output S,
  output Cout
);

  wire and_1_out, and_2_out, xor_1_out;

  xor xor_1 (xor_1_out, A, B);
  and and_1 (and_1_out, A, B);
  xor xor_2 (S, xor_1_out, Cin);
  and and_2 (and_2_out, xor_1_out, Cin);
  or or_1 (Cout, and_2_out, and_1_out);
endmodule

module sumador_4 (
  input  Cin,
  input  [3:0] A,
  input  [3:0] B,
  output [3:0] S,
  output Cout
);

  wire sumador_completo_1_cout, sumador_completo_2_cout, sumador_completo_3_cout;

  sumador_completo sumador_completo_1 (.Cin(Cin), .A(A[0]), .B(B[0]), .S(S[0]), .Cout(sumador_completo_1_cout));
  sumador_completo sumador_completo_2 (
    .Cin(sumador_completo_1_cout), .A(A[1]), .B(B[1]), .S(S[1]), .Cout(sumador_completo_2_cout));
  sumador_completo sumador_completo_3 (
    .Cin(sumador_completo_2_cout), .A(A[2]), .B(B[2]), .S(S[2]), .Cout(sumador_completo_3_cout));
  sumador_completo sumador_completo_4 (.Cin(sumador_completo_3_cout), .A(A[3]), .B(B[3]), .S(S[3]), .Cout(Cout));
  Hex_Digit_Display hex_digit_display_1 (.value(S));  // open: dp

  // Notes on the sheet:
  //   A: initial=0x1
endmodule

module comparador_cero (
  input  [3:0] A,
  output Z
);

  wire or_1_out, or_2_out, or_3_out;

  or or_1 (or_1_out, A[0], A[1]);
  or or_2 (or_2_out, A[2], A[3]);
  or or_3 (or_3_out, or_1_out, or_2_out);
  not not_1 (Z, or_3_out);
endmodule

module sumador_flags (
  input  Cin,
  input  [3:0] A,
  input  [3:0] B,
  output [3:0] S,
  output N,
  output Z,
  output V,
  output C
);

  wire not_1_out, xor_1_out, xor_2_out;

  xor xor_1 (xor_1_out, A[3], B[3]);
  not not_1 (not_1_out, xor_1_out);
  Hex_Digit_Display hex_digit_display_1 (.value({N, S[2:0]}));  // open: dp
  sumador_4 sumador_4_1 (.Cin(Cin), .A(A), .B(B), .S({N, S[2:0]}), .Cout(C));
  xor xor_2 (xor_2_out, N, B[3]);
  and and_1 (V, xor_2_out, not_1_out);
  comparador_cero comparador_cero_1 (.A({N, S[2:0]}), .Z(Z));

  assign S[3] = N;
endmodule

module incrementador_4 (
  input  [3:0] A,
  output [3:0] S
);

  sumador_4 sumador_4_1 (.Cin(1'b0), .A(A), .B(4'b0001), .S(S));  // open: Cout
  Hex_Digit_Display hex_digit_display_1 (.value(S));  // open: dp
endmodule

module inversor_4 (
  input  [3:0] A,
  input  INV,
  output [3:0] S
);

  wire [3:0] xor_1_out;

  xor xor_1 (xor_1_out[0], A[0], INV);
  xor xor_2 (xor_1_out[1], A[1], INV);
  xor xor_3 (xor_1_out[2], A[2], INV);
  xor xor_4 (xor_1_out[3], A[3], INV);
  Hex_Digit_Display hex_digit_display_1 (.value(S));  // open: dp
  sumador_4 sumador_4_1 (.Cin(INV), .A(xor_1_out), .B(4'b0000), .S(S));  // open: Cout
endmodule

module ALU (
  input  [3:0] A,
  input  [3:0] B,
  input  [1:0] OP,
  output N,
  output Z,
  output V,
  output C,
  output [3:0] S
);

  wire restador_flags_1_c, restador_flags_1_n, restador_flags_1_v, restador_flags_1_z, sumador_flags_1_c,
       sumador_flags_1_n, sumador_flags_1_v, sumador_flags_1_z;
  wire [3:0] ambita_1_out_3, orbita_1_out_3, restador_flags_1_r, sumador_flags_1_s;

  restador_flags restador_flags_1 (
    .A(A), .B(B), .r(restador_flags_1_r), .N(restador_flags_1_n), .Z(restador_flags_1_z),
    .V(restador_flags_1_v), .C(restador_flags_1_c));
  sumador_flags sumador_flags_1 (
    .Cin(1'b0), .A(A), .B(B), .S(sumador_flags_1_s), .N(sumador_flags_1_n), .Z(sumador_flags_1_z),
    .V(sumador_flags_1_v), .C(sumador_flags_1_c));
  orbita orbita_1 (.A(A), .B(B), .out_3(orbita_1_out_3));
  ambita ambita_1 (.A(A), .B(B), .out_3(ambita_1_out_3));
  Multiplexer #(.select(2), .width(4)) multiplexer_1 (
    .in0(sumador_flags_1_s), .in1(restador_flags_1_r), .in2(ambita_1_out_3), .in3(orbita_1_out_3), .out(S),
    .sel(OP));
  Multiplexer #(.select(2)) multiplexer_2 (
    .in0(sumador_flags_1_n), .in1(restador_flags_1_n), .out(N), .sel(OP));  // open: in2, in3
  Multiplexer #(.select(2)) multiplexer_3 (
    .in0(sumador_flags_1_z), .in1(restador_flags_1_z), .out(Z), .sel(OP));  // open: in2, in3
  Multiplexer #(.select(2)) multiplexer_4 (
    .in0(sumador_flags_1_v), .in1(restador_flags_1_v), .out(V), .sel(OP));  // open: in2, in3
  Multiplexer #(.select(2)) multiplexer_5 (
    .in0(sumador_flags_1_c), .in1(restador_flags_1_c), .out(C), .sel(OP));  // open: in2, in3
  Hex_Digit_Display hex_digit_display_1 (.value(S));  // open: dp
endmodule

module verificador (
  output [3:0] out_1,
  output [3:0] out_2,
  output [1:0] out_3,
  output halt,
  output N,
  output Z,
  output V,
  output C,
  output [3:0] res
);

  wire clock_1_out;

  Clock clock_1 (.out(clock_1_out));
  Counter #(.max('h3ff), .width(10)) counter_1 (
    .clk(clock_1_out), .carry(halt), .Q({out_3, out_2, out_1}));  // open: clr, load, up, count, D
  ALU alu_1 (.A(out_1), .B(out_2), .OP(out_3), .N(N), .Z(Z), .V(V), .C(C), .S(res));
endmodule

module orbita (
  input  [3:0] A,
  input  [3:0] B,
  output [3:0] out_3
);

  or or_1 (out_3[0], A[0], B[0]);
  or or_2 (out_3[1], A[1], B[1]);
  or or_3 (out_3[2], A[2], B[2]);
  or or_4 (out_3[3], A[3], B[3]);
endmodule

module ambita (
  input  [3:0] A,
  input  [3:0] B,
  output [3:0] out_3
);

  and and_1 (out_3[0], A[0], B[0]);
  and and_2 (out_3[1], A[1], B[1]);
  and and_3 (out_3[2], A[2], B[2]);
  and and_4 (out_3[3], A[3], B[3]);
endmodule

module restador_flags (
  input  [3:0] A,
  input  [3:0] B,
  output [3:0] r,
  output N,
  output Z,
  output V,
  output C
);

  wire sumador_flags_1_c;
  wire [3:0] inversor_4_1_s;

  xor xor_1 (V, r[3], A[3]);
  inversor_4 inversor_4_1 (.A(B), .INV(1'b1), .S(inversor_4_1_s));
  sumador_flags sumador_flags_1 (
    .Cin(1'b0), .A(A), .B(inversor_4_1_s), .S(r), .N(N), .Z(Z), .C(sumador_flags_1_c));  // open: V
  not not_1 (C, sumador_flags_1_c);
endmodule
